// Digital circuit 4_bit register(Program Counter).dig as structural Verilog
module _4_bit_register_Program_Counter (
  input  C,
  input  [3:0] D,
  input  [1:0] Control,
  output [3:0] Output
);

  wire [3:0] add_1_s, multiplexer_1_out;

  Add #(.Bits(4)) add_1 (.a(Output), .b(4'b0000), .c_i(1'b1), .s(add_1_s));  // open: c_o
  Multiplexer #(.Selector_Bits(2), .Bits(4)) multiplexer_1 (
    .sel(Control), .in_0(D), .in_1(Output), .in_2(4'b0000), .in_3(add_1_s), .out(multiplexer_1_out));
  D_FF D3 (.D(multiplexer_1_out[3]), .C(C), .Q(Output[3]));  // open: nQ
  D_FF D2 (.D(multiplexer_1_out[2]), .C(C), .Q(Output[2]));  // open: nQ
  D_FF D1 (.D(multiplexer_1_out[1]), .C(C), .Q(Output[1]));  // open: nQ
  D_FF D0 (.D(multiplexer_1_out[0]), .C(C), .Q(Output[0]));  // open: nQ

  // Notes on the sheet:
  //   Control: 00 --> Load
  //   01 --> Hold
  //   10 --> Reset
  //   11 --> inc
endmodule
