// Digital circuit Assign(1)_Small Fetch_harness.dig as structural Verilog
module Assign_1__Small_Fetch_harness (
  input  INC,
  input  IR_LD,
  input  Clck,
  output [7:0] Output
);

  wire not_1_out;
  wire [3:0] _4_bit_register_program_counter____copy_1_p4;
  wire [7:0] memory_row_8_bit_long___assin_1____copy_1_p3;

  not not_1 (not_1_out, IR_LD);
  // memory_row_8_bit_long___Assin_1____Copy memory_row_8_bit_long___assin_1____copy_1: pin names not known; wires that end beside it: Clck, not_1_out, memory_row_8_bit_long___assin_1____copy_1_p3, Output
  // _4_bit_register_Program_Counter____Copy _4_bit_register_program_counter____copy_1: pin names not known; wires that end beside it: Clck, 4'b0000, {INC, 1'b1}, _4_bit_register_program_counter____copy_1_p4
  memory___16x8_Assin_1 memory___16x8_assin_1_1 (
    .Adress_PIN(_4_bit_register_program_counter____copy_1_p4), .Clck(Clck), .Input({8{1'b0}}),
    .control(1'b1), .Output(memory_row_8_bit_long___assin_1____copy_1_p3));
endmodule
