// Digital circuit memory - 16x4_Assin(1) .dig as structural Verilog
module memory___16x4_Assin_1 (
  input  [3:0] Adress_PIN,
  input  Clck,
  input  [3:0] Input,
  input  control,
  output [3:0] Output
);

  wire and_1_out, and_2_out, and_3_out, and_4_out, and_5_out, and_6_out, and_7_out, and_8_out, and_9_out,
       and_10_out, and_11_out, and_12_out, and_13_out, and_14_out, and_15_out, and_16_out, decoder_1_out_0,
       decoder_1_out_1, decoder_1_out_2, decoder_1_out_3, decoder_1_out_4, decoder_1_out_5, decoder_1_out_6,
       decoder_1_out_7, decoder_1_out_8, decoder_1_out_9, decoder_1_out_10, decoder_1_out_11,
       decoder_1_out_12, decoder_1_out_13, decoder_1_out_14, decoder_1_out_15;
  wire [3:0] memory_row_4_bit_long_1_p4, memory_row_4_bit_long_2_p4, memory_row_4_bit_long_3_p4,
       memory_row_4_bit_long_4_p4, memory_row_4_bit_long_5_p4, memory_row_4_bit_long_6_p4,
       memory_row_4_bit_long_7_p4, memory_row_4_bit_long_8_p4, memory_row_4_bit_long_9_p4,
       memory_row_4_bit_long_10_p4, memory_row_4_bit_long_11_p4, memory_row_4_bit_long_12_p4,
       memory_row_4_bit_long_13_p4, memory_row_4_bit_long_14_p4, memory_row_4_bit_long_15_p4,
       memory_row_4_bit_long_16_p4;

  Decoder #(.Selector_Bits(4)) decoder_1 (
    .sel(Adress_PIN), .out_0(decoder_1_out_0), .out_1(decoder_1_out_1), .out_2(decoder_1_out_2),
    .out_3(decoder_1_out_3), .out_4(decoder_1_out_4), .out_5(decoder_1_out_5), .out_6(decoder_1_out_6),
    .out_7(decoder_1_out_7), .out_8(decoder_1_out_8), .out_9(decoder_1_out_9), .out_10(decoder_1_out_10),
    .out_11(decoder_1_out_11), .out_12(decoder_1_out_12), .out_13(decoder_1_out_13),
    .out_14(decoder_1_out_14), .out_15(decoder_1_out_15));
  and and_1 (and_1_out, Clck, decoder_1_out_0);
  and and_2 (and_2_out, Clck, decoder_1_out_1);
  and and_3 (and_3_out, Clck, decoder_1_out_2);
  and and_4 (and_4_out, Clck, decoder_1_out_3);
  and and_5 (and_5_out, Clck, decoder_1_out_4);
  and and_6 (and_6_out, Clck, decoder_1_out_5);
  and and_7 (and_7_out, Clck, decoder_1_out_6);
  and and_8 (and_8_out, Clck, decoder_1_out_7);
  and and_9 (and_9_out, Clck, decoder_1_out_8);
  and and_10 (and_10_out, Clck, decoder_1_out_9);
  and and_11 (and_11_out, Clck, decoder_1_out_10);
  and and_12 (and_12_out, Clck, decoder_1_out_11);
  and and_13 (and_13_out, Clck, decoder_1_out_12);
  and and_14 (and_14_out, Clck, decoder_1_out_13);
  and and_15 (and_15_out, Clck, decoder_1_out_14);
  and and_16 (and_16_out, Clck, decoder_1_out_15);
  // memory_row_4_bit_long memory_row_4_bit_long_1: pin names not known; wires that end beside it: and_1_out, control, Input, memory_row_4_bit_long_1_p4
  // memory_row_4_bit_long memory_row_4_bit_long_2: pin names not known; wires that end beside it: and_2_out, control, Input, memory_row_4_bit_long_2_p4
  // memory_row_4_bit_long memory_row_4_bit_long_3: pin names not known; wires that end beside it: and_3_out, control, Input, memory_row_4_bit_long_3_p4
  // memory_row_4_bit_long memory_row_4_bit_long_4: pin names not known; wires that end beside it: and_4_out, control, Input, memory_row_4_bit_long_4_p4
  // memory_row_4_bit_long memory_row_4_bit_long_5: pin names not known; wires that end beside it: and_5_out, control, Input, memory_row_4_bit_long_5_p4
  // memory_row_4_bit_long memory_row_4_bit_long_6: pin names not known; wires that end beside it: and_6_out, control, Input, memory_row_4_bit_long_6_p4
  // memory_row_4_bit_long memory_row_4_bit_long_7: pin names not known; wires that end beside it: and_7_out, control, Input, memory_row_4_bit_long_7_p4
  // memory_row_4_bit_long memory_row_4_bit_long_8: pin names not known; wires that end beside it: and_8_out, control, Input, memory_row_4_bit_long_8_p4
  // memory_row_4_bit_long memory_row_4_bit_long_9: pin names not known; wires that end beside it: and_9_out, control, Input, memory_row_4_bit_long_9_p4
  // memory_row_4_bit_long memory_row_4_bit_long_10: pin names not known; wires that end beside it: and_10_out, control, Input, memory_row_4_bit_long_10_p4
  // memory_row_4_bit_long memory_row_4_bit_long_11: pin names not known; wires that end beside it: and_11_out, control, Input, memory_row_4_bit_long_11_p4
  // memory_row_4_bit_long memory_row_4_bit_long_12: pin names not known; wires that end beside it: and_12_out, control, Input, memory_row_4_bit_long_12_p4
  // memory_row_4_bit_long memory_row_4_bit_long_13: pin names not known; wires that end beside it: and_13_out, control, Input, memory_row_4_bit_long_13_p4
  // memory_row_4_bit_long memory_row_4_bit_long_14: pin names not known; wires that end beside it: and_14_out, control, Input, memory_row_4_bit_long_14_p4
  // memory_row_4_bit_long memory_row_4_bit_long_15: pin names not known; wires that end beside it: and_15_out, control, Input, memory_row_4_bit_long_15_p4
  // memory_row_4_bit_long memory_row_4_bit_long_16: pin names not known; wires that end beside it: and_16_out, control, Input, memory_row_4_bit_long_16_p4
  Multiplexer #(.Selector_Bits(4), .Bits(4)) multiplexer_1 (
    .sel(Adress_PIN), .in_0(memory_row_4_bit_long_1_p4), .in_1(memory_row_4_bit_long_2_p4),
    .in_2(memory_row_4_bit_long_3_p4), .in_3(memory_row_4_bit_long_4_p4), .in_4(memory_row_4_bit_long_5_p4),
    .in_5(memory_row_4_bit_long_6_p4), .in_6(memory_row_4_bit_long_7_p4), .in_7(memory_row_4_bit_long_8_p4),
    .in_8(memory_row_4_bit_long_9_p4), .in_9(memory_row_4_bit_long_10_p4),
    .in_10(memory_row_4_bit_long_11_p4), .in_11(memory_row_4_bit_long_12_p4),
    .in_12(memory_row_4_bit_long_13_p4), .in_13(memory_row_4_bit_long_14_p4),
    .in_14(memory_row_4_bit_long_15_p4), .in_15(memory_row_4_bit_long_16_p4), .out(Output));
endmodule
