// Digital circuit memory_row_8 bit long - Assin(1).dig as structural Verilog
module memory_row_8_bit_long___Assin_1 (
  input  Clck,
  input  control,
  input  [11:0] Input,
  output [11:0] Output
);

  wire [11:0] multiplexer_1_out;

  Multiplexer #(.Bits(12)) multiplexer_1 (.sel(control), .in_0(Input), .in_1(Output), .out(multiplexer_1_out));
  D_FF D11 (.D(multiplexer_1_out[11]), .C(Clck), .Q(Output[11]));  // open: nQ
  D_FF D10 (.D(multiplexer_1_out[10]), .C(Clck), .Q(Output[10]));  // open: nQ
  D_FF D9 (.D(multiplexer_1_out[9]), .C(Clck), .Q(Output[9]));  // open: nQ
  D_FF D8 (.D(multiplexer_1_out[8]), .C(Clck), .Q(Output[8]));  // open: nQ
  D_FF D7 (.D(multiplexer_1_out[7]), .C(Clck), .Q(Output[7]));  // open: nQ
  D_FF D6 (.D(multiplexer_1_out[6]), .C(Clck), .Q(Output[6]));  // open: nQ
  D_FF D5 (.D(multiplexer_1_out[5]), .C(Clck), .Q(Output[5]));  // open: nQ
  D_FF D4 (.D(multiplexer_1_out[4]), .C(Clck), .Q(Output[4]));  // open: nQ
  D_FF D3 (.D(multiplexer_1_out[3]), .C(Clck), .Q(Output[3]));  // open: nQ
  D_FF D2 (.D(multiplexer_1_out[2]), .C(Clck), .Q(Output[2]));  // open: nQ
  D_FF D1 (.D(multiplexer_1_out[1]), .C(Clck), .Q(Output[1]));  // open: nQ
  D_FF D0 (.D(multiplexer_1_out[0]), .C(Clck), .Q(Output[0]));  // open: nQ

  // Notes on the sheet:
  //   control: 0 --> Write
  //   1 --> Hold
endmodule
